# Fritzing sketch Modem 1 (saved by Fritzing 0.9.3b)
breadboards: 1

parts:
  Part1 = Adafruit T-Cobbler Plus [part_number="Adafruit #1989 and #2028"]  # not connected
  HS = LED - 5mm [color="Red (633nm)" package="5 mm [THT]"]
  MR = LED - 5mm [color="Red (633nm)" package="5 mm [THT]"]
  R1 = Resistor [tolerance=±5% resistance=220 package=THT]
  R2 = Resistor [tolerance=±5% resistance=220 package=THT]
  RI = LED - 5mm [color="Red (633nm)" package="5 mm [THT]"]
  R3 = Resistor [tolerance=±5% resistance=220 package=THT]
  OH = LED - 5mm [color="Red (633nm)" package="5 mm [THT]"]
  R4 = Resistor [tolerance=±5% resistance=220 package=THT]
  TR = LED - 5mm [color="Red (633nm)" package="5 mm [THT]"]
  R5 = Resistor [tolerance=±5% resistance=220 package=THT]
  RD = LED - 5mm [color="Red (633nm)" package="5 mm [THT]"]
  R6 = Resistor [tolerance=±5% resistance=220 package=THT]
  CS = LED - 5mm [color="Red (633nm)" package="5 mm [THT]"]
  R7 = Resistor [tolerance=±5% resistance=220 package=THT]
  SD = LED - 5mm [color="Red (633nm)" package="5 mm [THT]"]
  R8 = Resistor [tolerance=±5% resistance=220 package=THT]
  AA = LED - 5mm [color="Red (633nm)" package="5 mm [THT]"]
  R9 = Resistor [tolerance=±5% resistance=220 package=THT]
  CD = LED - 5mm [color="Red (633nm)" package="5 mm [THT]"]
  R10 = Resistor [tolerance=±5% resistance=220 package=THT]
  U1 = RS232 Transceiver [package=dil16]
  U2 = RS232 Transceiver [package=dil16]
  U3 = RS232 Transceiver [package=dil16]
  C1 = Capacitor [package=cap-pth-small2]
  C2 = Capacitor [package=cap-pth-small2]
  C3 = Capacitor [package=cap-pth-small2]
  C4 = Capacitor [package=cap-pth-large]
  C5 = Capacitor [package=cap-pth-large]
  C6 = Capacitor [package=cap-pth-large]
  C10 = Capacitor [package=cap-pth-large]
  C11 = Capacitor [package=cap-pth-large]
  C12 = Capacitor [package=cap-pth-large]
  C13 = Capacitor [package=cap-pth-large]
  C14 = Capacitor [package=cap-pth-large]
  C15 = Capacitor [package=cap-pth-large]
  X1 = DB9 Connector [package=db9]

nets:
  N1: HS.anode, R2.Pin_1
  N2: MR.anode, R1.Pin_0
  GND: R1.Pin_1, R5.Pin_1, R6.Pin_1, R7.Pin_1, R8.Pin_1, U1.GND, U2.GND, U3.GND, C4.2, C5.2, C6.2
  N3: R2.Pin_0, R3.Pin_0, R4.Pin_0, R9.Pin_0, R10.Pin_0, U1.V+, U1.V-, U2.V+, U2.V-, U3.V+, U3.V-, C10.1, C10.2, C11.1, C11.2, C12.1, C12.2, C13.1, C13.2, C14.1, C14.2, C15.1, C15.2, X1.5
  N4: RI.anode, R3.Pin_1
  N5: OH.anode, R4.Pin_1
  N6: TR.anode, R5.Pin_0
  N7: RD.anode, R6.Pin_0
  N8: CS.anode, R7.Pin_0
  N9: SD.anode, R8.Pin_0
  N10: AA.anode, R9.Pin_1
  N11: CD.anode, R10.Pin_1
  N12: U1.C1+, C3.2
  N13: U1.C1-, C3.1
  N14: U1.T2OUT, X1.3
  N15: U1.T1OUT, X1.1
  VCC: U1.VCC, U2.VCC, U3.VCC, C4.1, C5.1, C6.1
  N16: U2.C1+, C2.2
  N17: U2.C1-, C2.1
  N18: U2.T2OUT, X1.9
  N19: U2.R2IN, X1.6
  N20: U2.R1IN, X1.2
  N21: U2.T1OUT, X1.4
  N22: U3.C1+, C1.2
  N23: U3.C1-, C1.1
  N24: U3.R1IN, X1.8
  N25: U3.T1OUT, X1.7

custom parts:
  Adafruit T-Cobbler Plus: The Raspberry Pi has landed on the Maker World like a 40-GPIO pinned, quad-USB ported, credit card sized bomb of DIY joy. And while you can use most of our great Model B accessories by hooking up our downgrade cable, its probably a good time to upgrade your set up and accessorize using all of the 40 pins. That's why we now carry the Assembled Adafruit Pi T-Cobbler Plus - Breakout + Cable for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
